// Logisim project 55298-55404.circ as structural Verilog: 1 circuit, main circuit main
module main (
  input  M1,
  input  M2,
  input  Botao,
  output \Doseador_de_café ,
  output \Bombas_de_água ,
  output \Doseador_de_açucar 
);

  wire and_1_out, and_2_out, and_3_out, and_4_out, and_5_out, and_6_out, and_7_out, and_8_out, and_9_out,
       and_10_out, and_11_out, and_12_out, and_13_out, and_16_out, and_17_out, and_18_out, CLK_out, D0_2_q,
       D0_2_qn, D0_q, D0_qn, D1_2_qn, D1_q, D1_qn, D2_q, D2_qn, not_1_out, not_2_out, or_1_out, or_2_out,
       or_3_out, or_4_out, or_5_out, or_6_out, or_7_out;

  Clock CLK (.out(CLK_out));
  not not_1 (not_1_out, M1);
  and and_1 (and_1_out, Botao, and_18_out);
  not not_2 (not_2_out, and_16_out);
  and and_2 (and_2_out, \Bombas_de_água , D0_2_q);
  and and_3 (and_3_out, D0_2_qn, D2_q);
  and and_4 (and_4_out, M1, D0_q);
  and and_5 (and_5_out, not_1_out, M2);
  and and_6 (and_6_out, not_2_out, D1_q);
  or or_1 (or_1_out, and_2_out, and_3_out);
  D_Flip_Flop D2 (.clk(CLK_out), .D(or_1_out), .Q(D2_q), .Qn(D2_qn));  // open: preset, en, reset
  D_Flip_Flop D1 (.clk(CLK_out), .D(or_2_out), .Q(D1_q), .Qn(D1_qn));  // open: preset, en, reset
  or or_2 (or_2_out, and_4_out, and_5_out, and_6_out);
  and and_7 (and_7_out, not_2_out, D1_q, D0_q);
  and and_8 (and_8_out, D2_qn, D0_2_q, D1_2_qn);
  or or_3 (or_3_out, and_8_out, and_9_out);
  and and_9 (and_9_out, D0_2_qn, \Bombas_de_água );
  and and_10 (and_10_out, not_1_out, D1_qn, D0_q);
  and and_11 (and_11_out, M1, D0_qn);
  and and_12 (and_12_out, M2, D1_q);
  D_Flip_Flop D1_2 (.clk(CLK_out), .D(or_3_out), .Q(\Bombas_de_água ), .Qn(D1_2_qn));  // open: preset, en, reset
  or or_4 (or_4_out, and_10_out, and_11_out, and_12_out, and_7_out);
  D_Flip_Flop D0 (.clk(CLK_out), .D(or_4_out), .Q(D0_q), .Qn(D0_qn));  // open: preset, en, reset
  and and_13 (and_13_out, and_1_out, D0_2_qn);
  D_Flip_Flop D0_2 (.clk(CLK_out), .D(and_13_out), .Q(D0_2_q), .Qn(D0_2_qn));  // open: preset, en, reset
  _7_Segment_Display u_7_segment_display_1 (
    .g(D1_q), .f(and_17_out), .a(or_7_out), .b(1'b1), .e(D0_qn), .d(or_5_out), .c(or_6_out));  // open: dp
  or or_5 (or_5_out, D1_q, D0_qn);
  and and_14 (\Doseador_de_café , D2_qn, D1_2_qn, D0_2_q);
  and and_15 (\Doseador_de_açucar , D2_q, D0_2_qn);
  and and_16 (and_16_out, D0_2_q, D1_2_qn, D2_q);
  and and_17 (and_17_out, D1_qn, D0_qn);
  or or_6 (or_6_out, D1_qn, D0_q);
  and and_18 (and_18_out, D1_q, D0_q);
  or or_7 (or_7_out, D1_q, D0_qn);
  LED Pronto_a_retirar (.in(and_16_out));
  LED Dinheiro_Suficiente (.in(and_18_out));
endmodule
